# Fritzing sketch schematic (saved by Fritzing 0.9.3b)
breadboards: 3

parts:
  Part1 = Arduino Uno (Rev3)
  LED1 = LED - 5mm [color="Red (633nm)" package="5 mm [THT]"]
  LED2 = LED - 5mm [color="Red (633nm)" package="5 mm [THT]"]
  LED3 = LED - 5mm [color="Yellow (595nm)" package="5 mm [THT]"]
  LED4 = LED - 5mm [color="Yellow (595nm)" package="5 mm [THT]"]
  LED5 = LED - 5mm [color="Green (565nm)" package="5 mm [THT]"]
  LED6 = LED - 5mm [color="Green (565nm)" package="5 mm [THT]"]
  R1 = Resistor [tolerance=±5% resistance=220 package=THT]
  R2 = Resistor [tolerance=±5% resistance=220 package=THT]
  R3 = Resistor [tolerance=±5% resistance=220 package=THT]
  R4 = Resistor [tolerance=±5% resistance=220 package=THT]
  R5 = Resistor [tolerance=±5% resistance=220 package=THT]
  R6 = Resistor [tolerance=±5% resistance=220 package=THT]
  S1 = Pushbutton [package="[THT]"]
  S2 = Pushbutton [package="[THT]"]
  HC-SR04_Sensor_2 = HC-SR04 Ultrasonic Distance Sensor
  R7 = Resistor [tolerance=±5% resistance=220 package=THT]
  R8 = Resistor [tolerance=±5% resistance=220 package=THT]
  HC-SR04_Sensor_1 = HC-SR04 Ultrasonic Distance Sensor

nets:
  N1: Part1.D8, R5.Pin_0
  N2: Part1.D9_PWM, R6.Pin_0
  N3: Part1.D10_PWM/SS, R3.Pin_0
  N4: Part1.D11_PWM/MOSI, R2.Pin_0
  N5: Part1.GND, LED1.cathode, LED2.cathode, LED3.cathode, LED4.cathode, LED5.cathode, LED6.cathode
  N6: Part1.D0/RX, HC-SR04_Sensor_1.TRIG
  N7: Part1.D1/TX, HC-SR04_Sensor_1.ECHO
  N8: Part1.D2, HC-SR04_Sensor_2.TRIG
  N9: Part1.D3_PWM, HC-SR04_Sensor_2.ECHO
  N10: Part1.D4, S2.Pin_3, S2.Pin_4
  N11: Part1.D5_PWM, S1.Pin_3, S1.Pin_4
  N12: Part1.D6_PWM, R1.Pin_0
  N13: Part1.D7, R4.Pin_0
  VCC: Part1.5V, HC-SR04_Sensor_2.VCC, R7.Pin_0, R8.Pin_0, HC-SR04_Sensor_1.VCC
  N14: LED1.anode, R1.Pin_1
  N15: LED2.anode, R6.Pin_1
  N16: LED3.anode, R4.Pin_1
  N17: LED4.anode, R3.Pin_1
  N18: LED5.anode, R5.Pin_1
  N19: LED6.anode, R2.Pin_1
  GND: S1.Pin_1, S1.Pin_2, HC-SR04_Sensor_2.GND, R7.Pin_1, HC-SR04_Sensor_1.GND
  N20: S2.Pin_1, S2.Pin_2, R8.Pin_1
